// Digital circuit 4_to_1_wide_mux.dig as structural Verilog
module _4_to_1_wide_mux (
  input  [3:0] A,
  input  [3:0] B,
  input  [3:0] C,
  input  [3:0] D,
  input  [1:0] S,
  output [3:0] Q
);

  wire [3:0] _2_to_1_wide_mux_1_q, _2_to_1_wide_mux_2_q;

  _2_to_1_wide_mux _2_to_1_wide_mux_1 (.A(A), .B(B), .Q(_2_to_1_wide_mux_1_q), .SEL(S[0]));
  _2_to_1_wide_mux _2_to_1_wide_mux_2 (.A(C), .B(D), .Q(_2_to_1_wide_mux_2_q), .SEL(S[0]));
  _2_to_1_wide_mux _2_to_1_wide_mux_3 (.A(_2_to_1_wide_mux_1_q), .B(_2_to_1_wide_mux_2_q), .Q(Q), .SEL(S[1]));
endmodule

/* Test case:
    A B C D S Q
loop(i, 250)
    let x = random(1<<4);
    let y = random(1<<4);
    let z = random(1<<4);
    let w = random(1<<4);
    (x) (y) (z) (w) (00) (x)
    (x) (y) (z) (w) (01) (y)
    (x) (y) (z) (w) (10) (z)
    (x) (y) (z) (w) (11) (w)
end loop
*/
