// Digital circuit full-adder.dig as structural Verilog
module full_adder (
  input  A,
  input  B,
  input  C_IN,
  output Q,
  output C_OUT
);

  // NotConnected on Q
  // NotConnected on C_OUT

  // Notes on the sheet:
  //   A: First bit input
  //   B: Second bit input
  //   C_IN: Input carry bit
  //   Q: Result of adding A, B, and C_IN
  //   C_OUT: Bit to indicate a carry occurred when adding A, B, and C_IN
endmodule

/* Test case Full-adder:
A B C_IN Q C_OUT
0 0 0 0 0
0 0 1 1 0
0 1 0 1 0
0 1 1 0 1
1 0 0 1 0
1 0 1 0 1
1 1 0 0 1
1 1 1 1 1
*/
