// Digital circuit half-adder.dig as structural Verilog
module half_adder (
  input  A,
  input  B,
  output Q,
  output C
);

  // NotConnected on Q
  // NotConnected on C

  // Notes on the sheet:
  //   A: First input bit
  //   B: Second input bit
  //   Q: Result of adding A and B
  //   C: Indicate that adding A and B produced a carry
endmodule

/* Test case Half-adder:
A B Q C
0 0 0 0 
0 1 1 0
1 0 1 0
1 1 0 1
*/
