// Digital circuit ripple-carry-adder.dig as structural Verilog
module ripple_carry_adder (
  input  [3:0] A,
  input  [3:0] B,
  output [3:0] Q
);

  // NotConnected on Q

  // Notes on the sheet:
  //   A: First adder input
  //   B: Second adder input
  //   Q: Result of adding A and B
endmodule

/* Test case Adder:
A B Q

loop(a, 1 << 4)
loop(b, 1 << 4)

(a) (b) ((a + b) & 0xF)

end loop
end loop
*/
