// Digital circuit counter.dig as structural Verilog
module counter (
  input  [15:0] D,
  input  ld,
  input  clk,
  output [15:0] Q
);

  // NotConnected on Q
endmodule

/* Test case:
clk ld D Q

0 0 0 0
c 0 0 0x1
c 0 0 0x2
*/
