// Digital circuit d_flipflop_with_en.dig as structural Verilog
module d_flipflop_with_en (
  input  clk,
  input  D,
  input  en,
  output Q
);

  // NotConnected on Q
endmodule

/* Test case:
clk en D Q
0 1 0 x
1 1 0 0
1 1 0 0
0 1 0 0
0 1 1 0
1 1 1 1
1 1 1 1
0 1 1 1
0 1 0 1
1 1 0 0
1 1 0 0
0 1 0 0
0 0 1 0
1 0 1 0
1 0 1 0
0 0 0 0
0 1 1 0
1 1 1 1
1 1 0 1
0 1 0 1
0 0 0 1
1 0 0 1
1 1 0 1
0 1 0 1
0 1 0 1
*/
