// Digital circuit d_latch.dig as structural Verilog
module d_latch (
  input  en,
  input  D,
  output Q
);

  // NotConnected on Q
endmodule

/* Test case:
en D Q
0 0 x
1 0 0
0 0 0
1 1 1
0 1 1
0 0 1
1 0 0
1 1 1
0 1 1
0 0 1
1 1 1
0 0 1
*/
