// Digital circuit incrementer.dig as structural Verilog
module incrementer (
  input  clk
);

  wire [3:0] add_1_s, d_latch_1_q;

  Add #(.Bits(4)) add_1 (.a(d_latch_1_q), .b(4'b0001), .c_i(1'b0), .s(add_1_s));  // open: c_o
  d_latch d_latch_1 (.en(clk), .D(add_1_s[0]), .Q(d_latch_1_q[0]));
  d_latch d_latch_2 (.en(clk), .D(add_1_s[1]), .Q(d_latch_1_q[1]));
  d_latch d_latch_3 (.en(clk), .D(add_1_s[2]), .Q(d_latch_1_q[2]));
  d_latch d_latch_4 (.en(clk), .D(add_1_s[3]), .Q(d_latch_1_q[3]));
endmodule
