// Digital circuit reg_file.dig as structural Verilog
module reg_file (
  input  [15:0] IN,
  input  clk,
  input  [2:0] WS,
  input  WE,
  input  [2:0] RS1,
  input  [2:0] RS2,
  output [15:0] OUT1,
  output [15:0] OUT2
);

  wire demultiplexer_1_out_1, demultiplexer_1_out_2, demultiplexer_1_out_3, demultiplexer_1_out_4;
  wire [15:0] notconnected_1_out, notconnected_2_out, notconnected_3_out, notconnected_4_out,
       notconnected_5_out, notconnected_6_out, register_1_q, register_2_q, register_3_q, register_4_q;

  Demultiplexer #(.Selector_Bits(3)) demultiplexer_1 (
    .sel(WS), .in(WE), .out_1(demultiplexer_1_out_1), .out_2(demultiplexer_1_out_2),
    .out_3(demultiplexer_1_out_3), .out_4(demultiplexer_1_out_4));  // open: out_0, out_5, out_6, out_7
  Register #(.Bits(16)) register_1 (.D(IN), .C(clk), .en(demultiplexer_1_out_1), .Q(register_1_q));
  Register #(.Bits(16)) register_2 (.D(IN), .C(clk), .en(demultiplexer_1_out_2), .Q(register_2_q));
  Register #(.Bits(16)) register_3 (.D(IN), .C(clk), .en(demultiplexer_1_out_3), .Q(register_3_q));
  Register #(.Bits(16)) register_4 (.D(IN), .C(clk), .en(demultiplexer_1_out_4), .Q(register_4_q));
  Multiplexer #(.Selector_Bits(3), .Bits(16)) multiplexer_1 (
    .sel(RS1), .in_0({16{1'b0}}), .in_1(register_1_q), .in_2(register_2_q), .in_3(register_3_q),
    .in_4(register_4_q), .in_5(notconnected_6_out), .in_6(notconnected_5_out), .in_7(notconnected_4_out),
    .out(OUT1));
  // NotConnected on notconnected_1_out
  // NotConnected on notconnected_2_out
  // NotConnected on notconnected_3_out
  // NotConnected on notconnected_4_out
  // NotConnected on notconnected_5_out
  // NotConnected on notconnected_6_out
  Multiplexer #(.Selector_Bits(3), .Bits(16)) multiplexer_2 (
    .sel(RS2), .in_0({16{1'b0}}), .in_1(register_1_q), .in_2(register_2_q), .in_3(register_3_q),
    .in_4(register_4_q), .in_5(notconnected_1_out), .in_6(notconnected_2_out), .in_7(notconnected_3_out),
    .out(OUT2));

  // Notes on the sheet:
  //   IN: The value to be saved into the register specified by WS if WE is high,
  //   WS: The index of the register which should save the value on IN on the next clock cycle (if WE is high).
  //   WE: Whether the register selected by WS should save the value from IN on the next cycle.
  //   RS1: The index of the register which should output its value to OUT1.
  //   OUT1: The value in the register specified by RS1.
  //   OUT2: The value in the register specified by RS2.
  //   RS2: The index of the register which should output its value to OUT2.
endmodule

/* Test case:
clk RS1 RS2 WS WE IN OUT1 OUT2
c 0 0 0 1 0x1234 0x1234 0x1234
c 1 0 1 1 0xBEEF 0xBEEF 0x1234
c 2 1 2 1 0xDEAD 0xDEAD 0xBEEF
c 3 2 3 1 0xFFFF 0xFFFF 0xDEAD
c 3 2 3 0 0xABCD 0xFFFF 0xDEAD
c 3 2 2 0 0xABCD 0xFFFF 0xDEAD
c 1 0 1 0 0xABCD 0xBEEF 0x1234
c 1 0 0 0 0xABCD 0xBEEF 0x1234
c 1 0 2 1 0xBADE 0xBEEF 0x1234
c 0 2 2 1 0xBADE 0x1234 0xBADE
c 0 0 2 0 0x1234 0x1234 0x1234
c 2 3 0 1 0x0000 0xBADE 0xFFFF
c 0 0 2 0 0x1234 0x0000 0x0000
*/
